# Fritzing sketch ataf (saved by Fritzing 0.9.2b)
breadboards: 1

parts:
  Componente1 = Arduino Uno (Rev3)
  LCD1 = LCD screen
  R2 = Resistor [tolerance=±5% resistance=220 package=THT]
  S1 = Pushbutton [package="[THT]"]
  R4 = Resistor [tolerance=±5% resistance=10k package=THT]
  R3 = Rotary Potentiometer (Small) [maximum_resistance=100kΩ package=THT]

nets:
  N1: Componente1.D11_PWM/MOSI, LCD1.E
  N2: Componente1.D12/MISO, LCD1.RS
  N3: Componente1.D13/SCK, S1.Pin_1, S1.Pin_2, R4.Pin_1
  N4: Componente1.D2, LCD1.DB7
  N5: Componente1.D3_PWM, LCD1.DB6
  N6: Componente1.D4, LCD1.DB5
  N7: Componente1.D5_PWM, LCD1.DB4
  5V: Componente1.5V, LCD1.VDD, R2.Pin_0, S1.Pin_3, S1.Pin_4, R3.leg1
  GND: Componente1.GND, LCD1.VSS, LCD1.R/W, LCD1.LED-, R4.Pin_0, R3.leg2
  N8: LCD1.V0, R3.wiper
  N9: LCD1.LED+, R2.Pin_1
